// Logisim project ALU.circ as structural Verilog: 1 circuit, main circuit ALU
module ALU (
  input  [15:0] x,
  input  [1:0] zx_nx,
  input  [15:0] y,
  input  f,
  input  no,
  input  [1:0] zy_ny,
  output ng,
  output [15:0] out,
  output zr
);

  wire Or16Way_out_2;
  wire [15:0] adder_1_out, and_1_out, multiplexer_1_out, multiplexer_2_out, multiplexer_3_out, not_1_out,
       not_2_out, not_3_out;

  assign not_1_out = ~x;  // NOT_Gate not_1, 16 bits wide
  assign not_2_out = ~y;  // NOT_Gate not_2, 16 bits wide
  Multiplexer #(.select(2), .width(16), .enable("false")) multiplexer_1 (
    .in0(x), .in1(not_1_out), .in2({16{1'b0}}), .in3({16{1'b1}}), .out(multiplexer_1_out), .sel(zx_nx));
  Multiplexer #(.select(2), .width(16), .enable("false")) multiplexer_2 (
    .in0(y), .in1(not_2_out), .in2({16{1'b0}}), .in3({16{1'b1}}), .out(multiplexer_2_out), .sel(zy_ny));
  assign and_1_out = multiplexer_1_out & multiplexer_2_out;  // AND_Gate and_1, 16 bits wide
  Adder #(.width(16)) adder_1 (.a(multiplexer_1_out), .b(multiplexer_2_out), .out(adder_1_out));  // open: cin, cout
  Multiplexer #(.width(16), .enable("false")) multiplexer_3 (
    .in0(and_1_out), .in1(adder_1_out), .out(multiplexer_3_out), .sel(f));
  assign not_3_out = ~multiplexer_3_out;  // NOT_Gate not_3, 16 bits wide
  Multiplexer #(.width(16), .enable("false")) multiplexer_4 (
    .in0(multiplexer_3_out), .in1(not_3_out), .out(out), .sel(no));
  Or16Way Or16Way (.in_1(out), .out_2(Or16Way_out_2));
  and and_2 (ng, out[15], 1'b1);
  not not_4 (zr, Or16Way_out_2);
endmodule
