// Logisim project Register.circ as structural Verilog: 1 circuit, main circuit main
module main (
  input  [15:0] Input,
  input  Load,
  output [15:0] Output
);

  wire clock_1_out;

  Clock clock_1 (.out(clock_1_out));
  Register #(.width(1)) register_1 (.D(Input[6]), .en(Load), .Q(Output[6]), .clk(clock_1_out));  // open: clr
  Register #(.width(1)) register_2 (.D(Input[7]), .en(Load), .Q(Output[7]), .clk(clock_1_out));  // open: clr
  Register #(.width(1)) register_3 (.D(Input[9]), .en(Load), .Q(Output[9]), .clk(clock_1_out));  // open: clr
  Register #(.width(1)) register_4 (.D(Input[8]), .en(Load), .Q(Output[8]), .clk(clock_1_out));  // open: clr
  Register #(.width(1)) register_5 (.D(Input[5]), .en(Load), .Q(Output[5]), .clk(clock_1_out));  // open: clr
  Register #(.width(1)) register_6 (.D(Input[10]), .en(Load), .Q(Output[10]), .clk(clock_1_out));  // open: clr
  Register #(.width(1)) register_7 (.D(Input[4]), .en(Load), .Q(Output[4]), .clk(clock_1_out));  // open: clr
  Register #(.width(1)) register_8 (.D(Input[11]), .en(Load), .Q(Output[11]), .clk(clock_1_out));  // open: clr
  Register #(.width(1)) register_9 (.D(Input[2]), .en(Load), .Q(Output[2]), .clk(clock_1_out));  // open: clr
  Register #(.width(1)) register_10 (.D(Input[3]), .en(Load), .Q(Output[3]), .clk(clock_1_out));  // open: clr
  Register #(.width(1)) register_11 (.D(Input[12]), .en(Load), .Q(Output[12]), .clk(clock_1_out));  // open: clr
  Register #(.width(1)) register_12 (.D(Input[13]), .en(Load), .Q(Output[13]), .clk(clock_1_out));  // open: clr
  Register #(.width(1)) register_13 (.D(Input[1]), .en(Load), .Q(Output[1]), .clk(clock_1_out));  // open: clr
  Register #(.width(1)) register_14 (.D(Input[14]), .en(Load), .Q(Output[14]), .clk(clock_1_out));  // open: clr
  Register #(.width(1)) register_15 (.D(Input[0]), .en(Load), .Q(Output[0]), .clk(clock_1_out));  // open: clr
  Register #(.width(1)) register_16 (.D(Input[15]), .en(Load), .Q(Output[15]), .clk(clock_1_out));  // open: clr

  // Notes on the sheet:
  //   16-bit Register
endmodule
